# Fritzing sketch _7SegDisplay (saved by Fritzing 0.9.2b)
breadboards: 1

parts:
  Part1 = Arduino Uno (Rev3)
  R1 = Resistor [tolerance=±5% resistance=220 package=THT]
  R2 = Resistor [tolerance=±5% resistance=220 package=THT]
  R3 = Resistor [tolerance=±5% resistance=220 package=THT]
  R4 = Resistor [tolerance=±5% resistance=220 package=THT]
  R7 = Resistor [tolerance=±5% resistance=220 package=THT]
  R6 = Resistor [tolerance=±5% resistance=220 package=THT]
  R5 = Resistor [tolerance=±5% resistance=220 package=THT]
  7_Segment_4_Digit_Display1 = 7-SEGMENT-4DIGIT common cathode [part_number=HS420561K-32 package=7-segment-4digit-cathode]

nets:
  N1: Part1.D8, R4.Pin_1
  N2: Part1.D10_PWM/SS, 7_Segment_4_Digit_Display1.pin_12
  N3: Part1.D11_PWM/MOSI, 7_Segment_4_Digit_Display1.pin_9
  N4: Part1.D12/MISO, 7_Segment_4_Digit_Display1.pin_8
  N5: Part1.D13/SCK, 7_Segment_4_Digit_Display1.pin_6
  N6: Part1.D2, R7.Pin_0
  N7: Part1.D3_PWM, R5.Pin_1
  N8: Part1.D4, R3.Pin_1
  N9: Part1.D5_PWM, R2.Pin_0
  N10: Part1.D6_PWM, R1.Pin_0
  N11: Part1.D7, R6.Pin_0
  N12: R1.Pin_1, 7_Segment_4_Digit_Display1.pin_1
  N13: R2.Pin_1, 7_Segment_4_Digit_Display1.pin_2
  N14: R3.Pin_0, 7_Segment_4_Digit_Display1.pin_4
  N15: R4.Pin_0, 7_Segment_4_Digit_Display1.pin_5
  N16: R7.Pin_1, 7_Segment_4_Digit_Display1.pin_11
  N17: R6.Pin_1, 7_Segment_4_Digit_Display1.pin_10
  N18: R5.Pin_0, 7_Segment_4_Digit_Display1.pin_7

custom parts:
  7-SEGMENT-4DIGIT common cathode: A 7 Segment 4 Digit common cathode display, with decimal points

// code stored in the sketch: _7SegDisplay.ino
/***********************************************************************
		Header Information
		Brody Ricketts
		Makecourse.com
		University of South Florida
***********************************************************************/

// Define segments on the 7-Segment Display
// Defined as the Segment address to the Arduino Address. ie Segment A on the 7-Segment Display
// is assisgned to digital pin 2 on the Arduino. 
#define A 2
#define B	3
#define C 4
#define D 5
#define E 6
#define F 7
#define G 8
#define DP 9 // Decimal Point is not used in this sketch.

//    _______ 
//   |	  A   |
// F |      | B
//   |--G---|
// E |      | C
//   |  D   |
//   _______


// Define the common Cathode pins. 
// The common cathode pins control the whole digits. 
#define CC1 10
#define CC2 11
#define CC3 12
#define CC4 13

// Define numberSegments
// numberSegments is an array to control the number displayed on the 7-Segment display
#define numberSegments 
{
	// {A, B, C, D, E, F, G, DP}
	{1, 1, 1, 1, 1, 1, 0, 0},\ // 0
	{0, 1, 1, 0, 0, 0, 0, 0},\ // 1
	{1, 1, 0, 1, 1, 0, 1, 0},\ // 2
	{1, 1, 1, 1, 0, 0, 1, 0},\ // 3
	{0, 1, 1, 0, 0, 1, 1, 0},\ // 4
	{1, 0, 1, 1, 0, 1, 1, 0},\ // 5
	{1, 0, 1, 1, 1, 1, 1, 0},\ // 6
	{1, 1, 1, 0, 0, 0, 0, 0},\ // 7
	{1, 1, 1, 1, 1, 1, 1, 0},\ // 8
	{1, 1, 1, 0, 0, 1, 1, 0}\ // 9
}

// Create a function to control the segments of the display
// Parameter digit is the digit of the display, ie 1-4
// the parameter time controls how long the segments are turned OFF
void setSegments(int number, int digit, int time)
{
	for(int seg = 0; seg < 8; seg++)
	{
		// Puts 5V to the anode of the segment if the numbers array shows a 1
		if(numbers[number][seg] == 1)
		{
			digitalWrite(segments[seg], HIGH);
		}
		// puts 0V to the anode of the segment if the numbers array shows a 0
		else
		{
			digitalWrite(segments[seg], LO);
		}
	}
	// Sets the voltage to the Common Cathode to 0V(LOW), ie the LEDs that have 5V at the anode, 
	// the number is diplayed
	digitalWrite(digit, LOW);
	// Set the on time, set in Microseconds. Or one millionth of a second. 0.000001
	delayMicroseconds(time);
	// Sets the Common Cathode to 5V(High), ie the LEDs are no longer visible.
	digitalWrite(digit, HIGH);
}

void setup()
{
	
}

void loop()
{
	
}
